# Fritzing sketch torreta (saved by Fritzing 0.9.3b)

parts:
  Arduino_Uno_R3 = Arduino Uno (Rev3)
  J1 = Basic Servo
  HC-SR04_Sensor_1 = HC-SR04 Ultrasonic Distance Sensor
  PIEZO = Piezo Speaker
  R1 = Resistor [tolerance=±5% resistance=220 package=THT]
  LED1 = LED - 5mm [color="Red (633nm)" package="5 mm [THT]"]
  LED2 = LED - 5mm [color="Red (633nm)" package="5 mm [THT]"]
  R2 = Resistor [tolerance=±5% resistance=220 package=THT]
  S1 = SWITCH-MOMENTARY-2 [package=tactile-switch-1101ne]
  S2 = SWITCH-MOMENTARY-2 [package=tactile-switch-1101ne]
  R3 = Resistor [tolerance=±5% resistance=4.7k package=THT]
  R4 = Resistor [tolerance=±5% resistance=4.7k package=THT]
  C1 = Electrolytic Capacitor [capacitance=100µF package="100 mil [THT, electrolytic]"]
  R5 = Resistor [tolerance=±5% resistance=220 package=THT]
  Q1 = NPN-Transistor [package="TO92 [THT]"]
  LED3 = LED - 5mm [color="Red (633nm)" package="5 mm [THT]"]
  R6 = Resistor [tolerance=±5% resistance=220 package=THT]
  LED4 = LED - 5mm [color="Red (633nm)" package="5 mm [THT]"]
  Q2 = NPN-Transistor [package="TO92 [THT]"]
  VCC1 = Battery block 9V
  ANT1 = Antenna
  ANT2 = Antenna
  S3 = SWITCH-MOMENTARY-2 [package=tactile-switch-1101ne]
  S4 = SWITCH-MOMENTARY-2 [package=tactile-switch-1101ne]

nets:
  N1: Arduino_Uno_R3.D8, S1.2, R3.Pin_0
  N2: Arduino_Uno_R3.D9_PWM, PIEZO.pin2
  N3: Arduino_Uno_R3.D10_PWM/SS, J1.pulse
  N4: Arduino_Uno_R3.D11_PWM/MOSI, HC-SR04_Sensor_1.TRIG
  N5: Arduino_Uno_R3.D12/MISO, HC-SR04_Sensor_1.GND
  GND: Arduino_Uno_R3.GND, J1.gnd, HC-SR04_Sensor_1.ECHO, R3.Pin_1, R4.Pin_1, C1.-, Q1.E, Q2.E, VCC1.-
  N6: Arduino_Uno_R3.D2, R5.Pin_0
  N7: Arduino_Uno_R3.D3_PWM, R6.Pin_0
  N8: Arduino_Uno_R3.D7, S2.2, R4.Pin_0
  VCC: Arduino_Uno_R3.5V, J1.vcc, HC-SR04_Sensor_1.VCC, PIEZO.pin1, R1.Pin_0, R2.Pin_0, C1.+
  N9: R1.Pin_1, LED1.anode
  N10: LED1.cathode, S1.1
  N11: LED2.cathode, S2.1
  N12: LED2.anode, R2.Pin_1
  N13: R5.Pin_1, LED3.anode
  N14: Q1.B, S3.1
  N15: Q1.C, Q2.C, VCC1.+, ANT1.antenna_lead, ANT2.antenna_lead
  N16: LED3.cathode, S3.2
  N17: R6.Pin_1, LED4.anode
  N18: LED4.cathode, S4.2
  N19: Q2.B, S4.1

// code stored in the sketch: torreta-1.0.0.ino
#include <math.h>

#define PIN_PIEZO 				3
#define PIN_SERVO 				5
#define PIN_SONAR_ECHO 		9
#define PIN_SONAR_TRIGGER 10

// PIEZO configuration
#define PIEZO_MIN_FREQ  100       //Buzzer minimum working frequency
#define PIEZO_MAX_FREQ  50000     //Buzzer maximum audible working frequency

// Global vars
long duration = 0;
long distance = 0;


void setup() {  
	makeNoise(5000, 50, 0, 1);
	randomSeed(analogRead(0));
	pinMode(PIN_SONAR_TRIGGER, OUTPUT);
	pinMode(PIN_SONAR_ECHO, INPUT);
	// pinMode(PIN_SERVO, OUTPUT);
	delay(1000);
	makeNoise(5000, 50, 150, 2);
	Serial.begin(9600);
}

void loop() {
	Serial.println(ping());
	//makeNoise(10000, 50, 1000 ,1);
	delay(1000);
}

long ping() {
	digitalWrite(PIN_SONAR_TRIGGER, LOW);
	delayMicroseconds(2);

	digitalWrite(PIN_SONAR_TRIGGER, HIGH);
	delayMicroseconds(10);
	digitalWrite(PIN_SONAR_TRIGGER, LOW);

	duration = pulseIn(PIN_SONAR_ECHO, HIGH);
	distance = duration * 0.034 / 2;

	return distance;
}

void makeNoise(int frequency, int duration, int wait, int times) {
  for(int i=0; i<times; i++) {
    tone(PIN_PIEZO, frequency, duration);
    delay(wait);
  }
}

// code stored in the sketch: torreta.ino
#include <math.h>
#include <Servo.h>

// SERVO configuration
const int PIN_SERVO 			= 4;
const int SERVO_MIN_ANGLE 		= 0;	//Servo minimun angle value
const int SERVO_CENTER_ANGLE 	= 90;	//Servo angle centered
const int SERVO_MAX_ANGLE 		= 180;	//Servo maximun angle value
const int SERVO_STEP 			= 1;	//Servo step size (in degrees)
const int SERVO_START_POSITION 	= 0;	//Servo start angle
bool servoDirection 			= 1;	// 0:left 1:right
int angle 						= 0;
int lastAngle 					= 0;
Servo myServo;

// SONAR configuration
const int PIN_SONAR_TRIGGER 	= 5;
const int PIN_SONAR_ECHO 		= 6;
int distance 					= 0;
int lastDistance 				= 0;

// PIEZO configuration
const int PIN_PIEZO 			= 3;
const int PIEZO_MIN_FREQ 		= 100;		//Buzzer minimun working frequency
const int PIEZO_MAX_FREQ 		= 50000;	//Buzzer maximun audible working frequency

// Switches
const int PIN_SWITCH_MASTER 	= 1;
bool switchMaster 				= false;
bool lastMasterState 			= false;
const int PIN_SWITCH_AUTO 		= 2;
bool switchAuto 				= false;
bool lastAutoState 				= false;

// Controllers
const int PIN_BUTTON_LEFT 		= 7;
bool turnLeft 					= false;
const int PIN_BUTTON_RIGHT 		= 8;
bool turnRight 					= false;

// Launchers
const int PIN_LAUNCHERS 		= [ 9, 10, 11, 12 ];
bool enabledLaunchers 			= [ false, false, false, false ];

// Data
byte flags = 0;


// Initial function
void setup() {  
	doNoise(5000, 50, 150, 1);
	Serial.begin(9600);
	randomSeed(analogRead(0));
	pinMode(PIN_SWITCH_MASTER, INPUT);
	pinMode(PIN_SWITCH_AUTO, INPUT);
	myServo.attach(PIN_SERVO);
	pinMode(PIN_SONAR_TRIGGER, OUTPUT);
	pinMode(PIN_SONAR_ECHO, INPUT);
	pinMode(PIN_BUTTON_LEFT, INPUT);
	pinMode(PIN_BUTTON_RIGHT, INPUT);
	configureLaunchers();
	servoResetPosition();
	doNoise(5000, 50, 150, 2);
}

// Main loop
void loop() {
	updateCurrentStatus();
	checkChanges();
	if(switchMaster) {
		// MASTER on
		if(switchAuto) {
			// AUTO mode
			doStep();
			updateServoAngle();
		} else {
			// MANUAL mode
			doStep();
			// TODO: implement here manual control
		}
	} else {
		// MASTER off
		startPosition();
		sendSerialData();
	}
}

void updateCurrentStatus() {
	// Save last status before change
	lastMasterState = switchMaster;
	lastAutoState = switchAuto;
	// Read and save current status
	switchMaster = digitalRead(PIN_SWITCH_MASTER);
	switchAuto = digitalRead(PIN_SWITCH_AUTO);
}

void checkChanges() {
	// Set SERVO to position 0 if MASTER change its status to ON
	if(switchMaster && !lastMasterState) {
		setServoAngle(SERVO_MIN_ANGLE);
	}
}

void configureLaunchers() {
	pinMode(PIN_LAUNCHER_1, OUTPUT);
	pinMode(PIN_LAUNCHER_2, OUTPUT);
	pinMode(PIN_LAUNCHER_3, OUTPUT);
	pinMode(PIN_LAUNCHER_4, OUTPUT);
	digitalWrite(PIN_LAUNCHER_1, launcher1Enabled);
	digitalWrite(PIN_LAUNCHER_2, launcher2Enabled);
	digitalWrite(PIN_LAUNCHER_3, launcher3Enabled);
	digitalWrite(PIN_LAUNCHER_4, launcher4Enabled);
}

void servoStartPosition() {
	setServoAngle(SERVO_MIN_ANGLE);
	lastAngle = SERVO_MIN_ANGLE;
}

void servoResetPosition() {
	setServoAngle(SERVO_CENTER_ANGLE);
	lastAngle = SERVO_CENTER_ANGLE;
}

void doStep() {
	setServoAngle(angle)
	delay(30);
	doPulse()
	sendSerialData();
}

void sendSerialData() {
	Serial.print(flags);
	Serial.print(':');
	Serial.print(angle);
	Serial.print(':');
	Serial.print(distance);
	Serial.print('.');
}

void updateServoAngle() {
	if(servoDirection) {
		servoAngle += SERVO_STEP;
	} else {
		servoAngle -= SERVO_STEP;
	}
	if(angle <= SERVO_MIN_ANGLE) {
		angle = SERVO_MIN_ANGLE;
		servoDirection = 1;
	} else if(angle >= SERVO_MAX_ANGLE) {
		angle = SERVO_MAX_ANGLE;
		servoDirection = 0;
	}
}

void setServoAngle(int newAngle) {
	myServo.write(newAngle);
	lastAngle = angle;
	angle = newAngle;
}

void doPulse() {
	long duration = 0;
	digitalWrite(PIN_SONAR_TRIGGER, LOW);
	delayMicroseconds(2);
	digitalWrite(PIN_SONAR_TRIGGER, HIGH);
	delayMicroseconds(10);
	digitalWrite(PIN_SONAR_TRIGGER, LOW);
	duration = pulseIn(PIN_SONAR_ECHO, HIGH);
	lastDistance = distance
	distance = duration * 0.034 / 2;
}

void doNoise(int frequency, int duration, int wait, int times) {
	for(int i=0; i<times; i++) {
		tone(PIN_PIEZO, frequency, duration);
		if(wait > 0) {
			delay(wait);
		}
  	}
}
